// Logisim project scrolling leds.circ as structural Verilog: 3 circuits, main circuit main
module main (
  input  [9:0] in_1,
  input  Enable
);

  wire button_1_out, clock_1_out, controlled_buffer_1_out, counter_1_carry;
  wire [6:0] keyboard_1_data;
  wire [9:0] adder_1_out, bit_extender_1_out, counter_1_q, multiplier_1_out, rom_1_data, shift_reg_1_out,
       shift_reg_1_out_5, shift_reg_1_out_6, shift_reg_1_out_7, shift_reg_1_out_8, shift_reg_1_out_9,
       shift_reg_1_out_10, shift_reg_1_out_11, shift_reg_1_out_12, shift_reg_1_out_13, shift_reg_2_out,
       shift_reg_2_out_5, shift_reg_2_out_6, shift_reg_2_out_7, shift_reg_2_out_8, shift_reg_2_out_9,
       shift_reg_2_out_10, shift_reg_2_out_11, shift_reg_2_out_12, shift_reg_2_out_13, shift_reg_3_out,
       shift_reg_3_out_5, shift_reg_3_out_6, shift_reg_3_out_7, shift_reg_3_out_8, shift_reg_3_out_9,
       shift_reg_3_out_10, shift_reg_3_out_11, shift_reg_3_out_12, shift_reg_3_out_13, shift_reg_4_out,
       shift_reg_4_out_5, shift_reg_4_out_6, shift_reg_4_out_7, shift_reg_4_out_8, shift_reg_4_out_9,
       shift_reg_4_out_10, shift_reg_4_out_11, shift_reg_4_out_12, shift_reg_4_out_13, shift_reg_5_out,
       shift_reg_5_out_5, shift_reg_5_out_6, shift_reg_5_out_7, shift_reg_5_out_8, shift_reg_5_out_9,
       shift_reg_5_out_10, shift_reg_5_out_11, shift_reg_5_out_12, shift_reg_5_out_13;

  Keyboard keyboard_1 (.clk(counter_1_carry), .clr(button_1_out), .data(keyboard_1_data));  // open: re, avail
  Button button_1 (.out(button_1_out));
  assign controlled_buffer_1_out = Enable ? clock_1_out : 1'bz;  // Controlled_Buffer controlled_buffer_1
  Clock clock_1 (.out(clock_1_out));
  Shift_Reg shift_reg_1 (
    .Reset(button_1_out), .Din(shift_reg_2_out), .clk(controlled_buffer_1_out), .out_6(shift_reg_1_out_6),
    .out_8(shift_reg_1_out_8), .out_10(shift_reg_1_out_10), .out_12(shift_reg_1_out_12),
    .out(shift_reg_1_out), .out_5(shift_reg_1_out_5), .out_7(shift_reg_1_out_7), .out_9(shift_reg_1_out_9),
    .out_11(shift_reg_1_out_11), .out_13(shift_reg_1_out_13));
  DotMatrix #(.matrixcols(10), .matrixrows(10)) dotmatrix_1 (
    .col0(shift_reg_1_out), .col1(shift_reg_1_out_5), .col2(shift_reg_1_out_7), .col3(shift_reg_1_out_9),
    .col4(shift_reg_1_out_11), .col5(shift_reg_1_out_13), .col6(shift_reg_1_out_12),
    .col7(shift_reg_1_out_10), .col8(shift_reg_1_out_8), .col9(shift_reg_1_out_6));
  DotMatrix #(.matrixcols(10), .matrixrows(10)) dotmatrix_2 (
    .col0(shift_reg_2_out), .col1(shift_reg_2_out_5), .col2(shift_reg_2_out_7), .col3(shift_reg_2_out_9),
    .col4(shift_reg_2_out_11), .col5(shift_reg_2_out_13), .col6(shift_reg_2_out_12),
    .col7(shift_reg_2_out_10), .col8(shift_reg_2_out_8), .col9(shift_reg_2_out_6));
  Shift_Reg shift_reg_2 (
    .Reset(button_1_out), .Din(shift_reg_3_out), .clk(controlled_buffer_1_out), .out_6(shift_reg_2_out_6),
    .out_8(shift_reg_2_out_8), .out_10(shift_reg_2_out_10), .out_12(shift_reg_2_out_12),
    .out(shift_reg_2_out), .out_5(shift_reg_2_out_5), .out_7(shift_reg_2_out_7), .out_9(shift_reg_2_out_9),
    .out_11(shift_reg_2_out_11), .out_13(shift_reg_2_out_13));
  assign bit_extender_1_out = {{3{1'b0}}, keyboard_1_data};  // Bit_Extender bit_extender_1
  Counter #(.width(10), .max('h5)) counter_1 (
    .Q(counter_1_q), .carry(counter_1_carry), .clk(controlled_buffer_1_out), .clr(button_1_out));  // open: load, D, count
  Multiplier #(.width(10)) multiplier_1 (.a(bit_extender_1_out), .b(in_1), .out(multiplier_1_out));  // open: cin, cout
  DotMatrix #(.matrixcols(10), .matrixrows(10)) dotmatrix_3 (
    .col0(shift_reg_3_out), .col1(shift_reg_3_out_5), .col2(shift_reg_3_out_7), .col3(shift_reg_3_out_9),
    .col4(shift_reg_3_out_11), .col5(shift_reg_3_out_13), .col6(shift_reg_3_out_12),
    .col7(shift_reg_3_out_10), .col8(shift_reg_3_out_8), .col9(shift_reg_3_out_6));
  Shift_Reg shift_reg_3 (
    .Reset(button_1_out), .Din(shift_reg_4_out), .clk(controlled_buffer_1_out), .out_6(shift_reg_3_out_6),
    .out_8(shift_reg_3_out_8), .out_10(shift_reg_3_out_10), .out_12(shift_reg_3_out_12),
    .out(shift_reg_3_out), .out_5(shift_reg_3_out_5), .out_7(shift_reg_3_out_7), .out_9(shift_reg_3_out_9),
    .out_11(shift_reg_3_out_11), .out_13(shift_reg_3_out_13));
  Adder #(.width(10)) adder_1 (.a(multiplier_1_out), .b(counter_1_q), .out(adder_1_out));  // open: cin, cout
  DotMatrix #(.matrixcols(10), .matrixrows(10)) dotmatrix_4 (
    .col0(shift_reg_4_out), .col1(shift_reg_4_out_5), .col2(shift_reg_4_out_7), .col3(shift_reg_4_out_9),
    .col4(shift_reg_4_out_11), .col5(shift_reg_4_out_13), .col6(shift_reg_4_out_12),
    .col7(shift_reg_4_out_10), .col8(shift_reg_4_out_8), .col9(shift_reg_4_out_6));
  Shift_Reg shift_reg_4 (
    .Reset(button_1_out), .Din(shift_reg_5_out), .clk(controlled_buffer_1_out), .out_6(shift_reg_4_out_6),
    .out_8(shift_reg_4_out_8), .out_10(shift_reg_4_out_10), .out_12(shift_reg_4_out_12),
    .out(shift_reg_4_out), .out_5(shift_reg_4_out_5), .out_7(shift_reg_4_out_7), .out_9(shift_reg_4_out_9),
    .out_11(shift_reg_4_out_11), .out_13(shift_reg_4_out_13));
  DotMatrix #(.matrixcols(10), .matrixrows(10)) dotmatrix_5 (
    .col0(shift_reg_5_out), .col1(shift_reg_5_out_5), .col2(shift_reg_5_out_7), .col3(shift_reg_5_out_9),
    .col4(shift_reg_5_out_11), .col5(shift_reg_5_out_13), .col6(shift_reg_5_out_12),
    .col7(shift_reg_5_out_10), .col8(shift_reg_5_out_8), .col9(shift_reg_5_out_6));
  ROM #(.addrWidth(10), .dataWidth(10)) rom_1 (.addr(adder_1_out), .data(rom_1_data));  // open: sel
  Shift_Reg shift_reg_5 (
    .Reset(button_1_out), .Din(rom_1_data), .clk(controlled_buffer_1_out), .out_6(shift_reg_5_out_6),
    .out_8(shift_reg_5_out_8), .out_10(shift_reg_5_out_10), .out_12(shift_reg_5_out_12),
    .out(shift_reg_5_out), .out_5(shift_reg_5_out_5), .out_7(shift_reg_5_out_7), .out_9(shift_reg_5_out_9),
    .out_11(shift_reg_5_out_11), .out_13(shift_reg_5_out_13));

  // Notes on the sheet:
  //   Reset
  //   Clock
  //   Scorlling LED's
  //   contents of rom_1 (hex, n*v repeats v):
  //   6*0 20 21 22 23 24 25 30 31 32 33 34 35 40 41 42 43 44 45 7f 3f 3f 3f 3c 170*0 180 3e8 180 0 0 0 300
  //   0 300 0 0 120 3f0 120 3f0 120 21*0 300 40*0 18 18 9*0 1f0 208 208 208 1f0 0 0 108 3f8 8 0 0 108 218
  //   228 248 188 0 110 208 248 248 1b0 0 60 a0 120 3f8 20 0 3d0 248 248 248 30 0 1f0 248 248 248 30 0 200
  //   200 278 280 300 0 1b0 248 248 248 1b0 0 188 248 248 248 1f0 43*0 1f8 220 220 220 1f8 0 3f8 248 248
  //   248 1b0 0 1f0 208 208 208 110 0 3f8 208 208 208 1f0 0 3f8 248 248 248 208 0 3f8 240 240 240 200 0
  //   1f0 208 208 228 130 0 3f8 40 40 40 3f8 0 0 208 3f8 208 0 0 10 8 8 8 3f0 0 3f8 40 a0 110 208 0 3f8
  //   4*8 0 3f8 100 80 100 3f8 0 3f8 180 40 30 3f8 0 1f0 208 208 208 1f0 0 3f8 240 240 240 180 0 1f0 208
  //   228 218 1f8 0 3f8 240 260 250 188 0 190 248 248 248 130 0 200 200 3f8 200 200 0 3f0 8 8 8 3f0 0 3e0
  //   10 8 10 3e0 0 3f0 8 70 8 3f0 0 208 1b0 40 1b0 208 0 200 100 f8 100 200 0 218 228 248 288 308 37*0 70
  //   88 88 f0 8 0 3f8 88 88 88 70 0 70 4*88 0 70 88 88 88 3f8 0 70 a8 a8 a8 48 0 0 88 1f8 288 0 0 72 89
  //   89 89 fe 0 3f8 80 80 80 78 0 0 88 2f8 8 0 0 0 2 81 2fe 0 0 3f8 20 50 88 0 0 0 208 3f8 8 0 0 f8 80 78
  //   80 78 0 f8 40 80 80 78 0 70 88 88 88 70 0 ff 88 88 88 70 0 70 88 88 88 ff 0 f8 40 80 80 40 0 48 a8
  //   a8 a8 90 0 0 80 3f0 88 0 0 f0 8 8 10 f8 0 e0 10 8 10 e0 0 f0 8 30 8 f0 0 88 50 20 50 88 0 f2 9 9 9
  //   fe 0 88 98 a8 c8 88
endmodule

module FIFO (
  input  [9:0] in_1
);

  RAM #(.addrWidth(10), .dataWidth(10), .bus("separate")) ram_1 (.din(in_1));  // open: addr, data, str, sel, clk, ld, clr
endmodule

module Shift_Reg (
  input  Reset,
  input  [9:0] Din,
  input  clk,
  output [9:0] out,
  output [9:0] out_5,
  output [9:0] out_6,
  output [9:0] out_7,
  output [9:0] out_8,
  output [9:0] out_9,
  output [9:0] out_10,
  output [9:0] out_11,
  output [9:0] out_12,
  output [9:0] out_13
);

  Register #(.width(10)) register_1 (.D(Din), .Q(out_6), .clk(clk), .clr(Reset));  // open: en
  Register #(.width(10)) register_2 (.D(out_6), .Q(out_8), .clk(clk), .clr(Reset));  // open: en
  Register #(.width(10)) register_3 (.D(out_8), .Q(out_10), .clk(clk), .clr(Reset));  // open: en
  Register #(.width(10)) register_4 (.D(out_10), .Q(out_12), .clk(clk), .clr(Reset));  // open: en
  Register #(.width(10)) register_5 (.D(out_12), .Q(out_13), .clk(clk), .clr(Reset));  // open: en
  Register #(.width(10)) register_6 (.D(out_11), .Q(out_9), .clk(clk), .clr(Reset));  // open: en
  Register #(.width(10)) register_7 (.D(out_13), .Q(out_11), .clk(clk), .clr(Reset));  // open: en
  Register #(.width(10)) register_8 (.D(out_9), .Q(out_7), .clk(clk), .clr(Reset));  // open: en
  Register #(.width(10)) register_9 (.D(out_7), .Q(out), .clk(clk), .clr(Reset));  // open: en

  assign out_5 = out;
endmodule
